# Fritzing sketch arduino_codebreaker (saved by Fritzing 0.9.4)
circuit board: 8.46667cm x 5.64444cm
breadboards: 3

parts:
  Part1 = HC-SR501 Body Sensor Module
  DHT1 = DHT11 Humitidy and Temperature Sensor
  R1 = Trimmer Potentiometer [maximum_resistance=10kΩ package=THT]
  R2 = Resistor [tolerance=±5% resistance=220 package="0603 [SMD]"]
  Mic1 = KY-038
  SERVO1 = Tower Pro SG90 servo [part_number=101246]
  YwRobot_Power_Supply1 = YwRobot Breadboard Power Supply [part_number=545043]
  LED1 = LEDs [package=led10mm]
  LCD1 = LCD screen
  Part2 = Arduino Uno (Rev3) - ICSP
  SG1 = Buzzer 12mm [package=buzzer-ccv-kit]
  Part3 = RFID-RC522-v2

nets:
  VDD: Part1.VCC, DHT1.VDD, R1.leg1, Mic1.pin3, YwRobot_Power_Supply1.VCC#5, LCD1.VDD, LCD1.LED+
  N1: Part1.OUT, Part2.A5/SCL
  GND: Part1.GND, DHT1.GND, R1.leg2, Mic1.pin2, YwRobot_Power_Supply1.GND#11, LED1.C, LCD1.VSS, LCD1.R/W, LCD1.LED-, SG1.2
  N2: DHT1.DATA, Part2.D2
  N3: R1.wiper, LCD1.V0
  N4: R2.Pin_0, LED1.A
  N5: R2.Pin_1, Part2.D10_PWM/SS
  N6: Mic1.pin4, Part2.A3
  N7: SERVO1.Signal, Part2.A0
  GND_2: SERVO1.GND, YwRobot_Power_Supply1.GND#13, Part3.IRQ, Part3.GND
  N8: YwRobot_Power_Supply1.VCC#9, Part3.3.3V
  N9: LCD1.RS, Part2.D9_PWM
  N10: LCD1.E, Part2.D8
  N11: LCD1.DB4, Part2.D3_PWM
  N12: LCD1.DB5, Part2.D4
  N13: LCD1.DB6, Part2.D6_PWM
  N14: LCD1.DB7, Part2.D7
  N15: Part2.A1, SG1.1
  N16: Part2.A4/SDA, Part3.SDA
  N17: Part2.D11_PWM/MOSI, Part3.MOSI
  N18: Part2.D12/MISO, Part3.MISO
  N19: Part2.D13/SCK, Part3.SCK
  N20: Part2.D5_PWM, Part3.RST

custom parts:
  HC-SR501 Body Sensor Module: Pyroelectric Infrared PIR Motion Sensor Detector Module
  DHT11 Humitidy and Temperature Sensor: DHT11 Humidity and Temperature Sensor
  KY-038: ky-038 Microphone sound sensor module
  Tower Pro SG90 servo: Original file by John De Cristofaro http://www.adafruit.com/products/1449 Adafruit Feedback Servo (Small) Edited by: e-radionica.com 28/9/2015
  YwRobot Breadboard Power Supply: The YwRobot Breadboard Power Supply (MB-V2) has two power rails; they can be 5V or 3V3. Power to the module can be provided through the female USB socket or through the A10 (female) 2.1mm power jack.
  RFID-RC522-v2: A simple China made RFID-RC522 Reader; do check the pin labels, as this is a MFRC522 based clone.
